// Logisim project RV32I.circ as structural Verilog
module main (
  input  [31:0] inPC,
  input  clk,
  input  [4:0] rsi1,
  input  [4:0] rsi2,
  input  [4:0] rdi,
  input  [31:0] rd,
  input  we,
  input  [31:0] dataA,
  input  [31:0] dataB,
  input  [3:0] sel,
  input  [31:0] ins,
  input  [2:0] ins_sel,
  output [31:0] outPCPlus4,
  output [31:0] outPC,
  output [31:0] rs1,
  output [31:0] rs2,
  output [31:0] dataD,
  output [31:0] imm31_0
);

  wire comparator_1_lt, comparator_2_lt, x0we_t, x1we_t, x2we_t, x3we_t, x4we_t, x5we_t, x6we_t, x7we_t,
       x8we_t, x9we_t, x10we_t, x11we_t, x12we_t, x13we_t, x14we_t, x15we_t, x16we_t, x17we_t, x18we_t,
       x19we_t, x20we_t, x21we_t, x22we_t, x23we_t, x24we_t, x25we_t, x26we_t, x27we_t, x28we_t, x29we_t,
       x30we_t, x31we_t;
  wire [31:0] addOut, andOut, orOut, sllOut, sltOut, sltuOut, sraOut, srlOut, subOut, x1q_t, x2q_t, x3q_t,
       x4q_t, x5q_t, x6q_t, x7q_t, x8q_t, x9q_t, x10q_t, x11q_t, x12q_t, x13q_t, x14q_t, x15q_t, x16q_t,
       x17q_t, x18q_t, x19q_t, x20q_t, x21q_t, x22q_t, x23q_t, x24_t, x24q_t, x25q_t, x26q_t, x27q_t, x28q_t,
       x29q_t, x30q_t, x31q_t, xorOut;

  Demultiplexer #(.select(5)) demultiplexer_1 (
    .out0(x0we_t), .out1(x1we_t), .out2(x2we_t), .out3(x3we_t), .out4(x4we_t), .out5(x5we_t), .out6(x6we_t),
    .out7(x7we_t), .out8(x8we_t), .out9(x9we_t), .out10(x10we_t), .out11(x11we_t), .out12(x12we_t),
    .out13(x13we_t), .out14(x14we_t), .out15(x15we_t), .out16(x16we_t), .out17(x17we_t), .out18(x18we_t),
    .out19(x19we_t), .out20(x20we_t), .out21(x21we_t), .out22(x22we_t), .out23(x23we_t), .out24(x24we_t),
    .out25(x25we_t), .out26(x26we_t), .out27(x27we_t), .out28(x28we_t), .out29(x29we_t), .out30(x30we_t),
    .out31(x31we_t), .in(we), .sel(rdi));
  Register #(.width(32)) register_1 (.D(inPC), .en(1'b1), .clk(clk), .Q(outPC));  // open: clr
  Register #(.width(32)) x4 (.D(rd), .en(x4we_t), .clk(clk), .Q(x4q_t));  // open: clr
  Register #(.width(32)) x8 (.D(rd), .en(x8we_t), .clk(clk), .Q(x8q_t));  // open: clr
  Register #(.width(32)) x12 (.D(rd), .en(x12we_t), .clk(clk), .Q(x12q_t));  // open: clr
  Register #(.width(32)) x16 (.D(rd), .en(x16we_t), .clk(clk), .Q(x16q_t));  // open: clr
  Register #(.width(32)) x20 (.D(rd), .en(x20we_t), .clk(clk), .Q(x20q_t));  // open: clr
  Register #(.width(32)) x24 (.D(rd), .en(x24we_t), .clk(clk), .Q(x24q_t));  // open: clr
  Register #(.width(32)) x28 (.D(rd), .en(x28we_t), .clk(clk), .Q(x28q_t));  // open: clr
  Adder #(.width(32)) adder_1 (.a(outPC), .b(32'h4), .out(outPCPlus4));  // open: cin, cout
  Register #(.width(32)) x1 (.D(rd), .en(x1we_t), .clk(clk), .Q(x1q_t));  // open: clr
  Register #(.width(32)) x5 (.D(rd), .en(x5we_t), .clk(clk), .Q(x5q_t));  // open: clr
  Register #(.width(32)) x9 (.D(rd), .en(x9we_t), .clk(clk), .Q(x9q_t));  // open: clr
  Register #(.width(32)) x13 (.D(rd), .en(x13we_t), .clk(clk), .Q(x13q_t));  // open: clr
  Register #(.width(32)) x17 (.D(rd), .en(x17we_t), .clk(clk), .Q(x17q_t));  // open: clr
  Register #(.width(32)) x21 (.D(rd), .en(x21we_t), .clk(clk), .Q(x21q_t));  // open: clr
  Register #(.width(32)) x25 (.D(rd), .en(x25we_t), .clk(clk), .Q(x25q_t));  // open: clr
  Register #(.width(32)) x29 (.D(rd), .en(x29we_t), .clk(clk), .Q(x29q_t));  // open: clr
  Adder #(.width(32)) adder_2 (.a(dataA), .b(dataB), .out(addOut));  // open: cin, cout
  Subtractor #(.width(32)) subtractor_1 (.a(dataA), .b(dataB), .out(subOut));  // open: bin, bout
  Shifter #(.width(32)) shifter_1 (.in(dataA), .\dist (dataB[4:0]), .out(sllOut));
  Comparator #(.width(32)) comparator_1 (.a(dataA), .b(dataB), .lt(comparator_1_lt));  // open: gt, eq
  Comparator #(.mode("unsigned"), .width(32)) comparator_2 (
    .a(dataA), .b(dataB), .lt(comparator_2_lt));  // open: gt, eq
  assign xorOut = dataA ^ dataB;  // XOR_Gate xor_1, 32 bits wide
  Shifter #(.shift("lr"), .width(32)) shifter_2 (.in(dataA), .\dist (dataB[4:0]), .out(srlOut));
  Shifter #(.shift("ar"), .width(32)) shifter_3 (.in(dataA), .\dist (dataB[4:0]), .out(sraOut));
  assign orOut = dataA | dataB;  // OR_Gate or_1, 32 bits wide
  assign andOut = dataA & dataB;  // AND_Gate and_1, 32 bits wide
  assign sltOut = {{31{1'b0}}, comparator_1_lt};  // Bit_Extender bit_extender_1
  assign sltuOut = {{31{1'b0}}, comparator_2_lt};  // Bit_Extender bit_extender_2
  Register #(.width(32)) x2 (.D(rd), .en(x2we_t), .clk(clk), .Q(x2q_t));  // open: clr
  Register #(.width(32)) x6 (.D(rd), .en(x6we_t), .clk(clk), .Q(x6q_t));  // open: clr
  Register #(.width(32)) x10 (.D(rd), .en(x10we_t), .clk(clk), .Q(x10q_t));  // open: clr
  Register #(.width(32)) x14 (.D(rd), .en(x14we_t), .clk(clk), .Q(x14q_t));  // open: clr
  Register #(.width(32)) x18 (.D(rd), .en(x18we_t), .clk(clk), .Q(x18q_t));  // open: clr
  Register #(.width(32)) x22 (.D(rd), .en(x22we_t), .clk(clk), .Q(x22q_t));  // open: clr
  Register #(.width(32)) x26 (.D(rd), .en(x26we_t), .clk(clk), .Q(x26q_t));  // open: clr
  Register #(.width(32)) x30 (.D(rd), .en(x30we_t), .clk(clk), .Q(x30q_t));  // open: clr
  Multiplexer #(.select(4), .width(32)) multiplexer_1 (
    .in0(addOut), .in1(sllOut), .in2(sltOut), .in3(sltuOut), .in4(xorOut), .in5(srlOut), .in6(orOut),
    .in7(andOut), .in8(subOut), .in13(sraOut), .out(dataD), .sel(sel));  // open: in9, in10, in11, in12, in14, in15
  Register #(.width(32)) x3 (.D(rd), .en(x3we_t), .clk(clk), .Q(x3q_t));  // open: clr
  Register #(.width(32)) x7 (.D(rd), .en(x7we_t), .clk(clk), .Q(x7q_t));  // open: clr
  Register #(.width(32)) x11 (.D(rd), .en(x11we_t), .clk(clk), .Q(x11q_t));  // open: clr
  Register #(.width(32)) x15 (.D(rd), .en(x15we_t), .clk(clk), .Q(x15q_t));  // open: clr
  Register #(.width(32)) x19 (.D(rd), .en(x19we_t), .clk(clk), .Q(x19q_t));  // open: clr
  Register #(.width(32)) x23 (.D(rd), .en(x23we_t), .clk(clk), .Q(x23q_t));  // open: clr
  Register #(.width(32)) x27 (.D(rd), .en(x27we_t), .clk(clk), .Q(x27q_t));  // open: clr
  Register #(.width(32)) x31 (.D(rd), .en(x31we_t), .clk(clk), .Q(x31q_t));  // open: clr
  Multiplexer #(.select(5), .width(32)) multiplexer_2 (
    .in0({32{1'b0}}), .in1(x1q_t), .in2(x2q_t), .in3(x3q_t), .in4(x4q_t), .in5(x5q_t), .in6(x6q_t),
    .in7(x7q_t), .in8(x8q_t), .in9(x9q_t), .in10(x10q_t), .in11(x11q_t), .in12(x12q_t), .in13(x13q_t),
    .in14(x14q_t), .in15(x15q_t), .in16(x16q_t), .in17(x17q_t), .in18(x18q_t), .in19(x19q_t), .in20(x20q_t),
    .in21(x21q_t), .in22(x22q_t), .in23(x23q_t), .in24(x24_t), .in25(x25q_t), .in26(x26q_t), .in27(x27q_t),
    .in28(x28q_t), .in29(x29q_t), .in30(x30q_t), .in31(x31q_t), .out(rs1), .sel(rsi1));
  Multiplexer #(.select(5), .width(32)) multiplexer_3 (
    .in0({32{1'b0}}), .in1(x1q_t), .in2(x2q_t), .in3(x3q_t), .in4(x4q_t), .in5(x5q_t), .in6(x6q_t),
    .in7(x7q_t), .in8(x8q_t), .in9(x9q_t), .in10(x10q_t), .in11(x11q_t), .in12(x12q_t), .in13(x13q_t),
    .in14(x14q_t), .in15(x15q_t), .in16(x16q_t), .in17(x17q_t), .in18(x18q_t), .in19(x19q_t), .in20(x20q_t),
    .in21(x21q_t), .in22(x22q_t), .in23(x23q_t), .in24(x24_t), .in25(x25q_t), .in26(x26q_t), .in27(x27q_t),
    .in28(x28q_t), .in29(x29q_t), .in30(x30q_t), .in31(x31q_t), .out(rs2), .sel(rsi2));

  // Other names for the same wires on the sheet: clk_t = clk; dataA_t[31:0] = dataA; dataB_t[31:0] = dataB;
  //   dataBL5_t[4:0] = dataB[4:0]; dataD_t[31:0] = dataD; imm31_0_t[31:0] = imm31_0; inPC_t[31:0] = inPC;
  //   ins_sel_t[2:0] = ins_sel; ins_t[31:0] = ins; outPC_t[31:0] = outPC; outPCPlus4_t[31:0] = outPCPlus4;
  //   rd_t[31:0] = rd; rdi_t[4:0] = rdi; rs1_t[31:0] = rs1; rs2_t[31:0] = rs2; rsi1_t[4:0] = rsi1; rsi2_t[4:0] = rsi2;
  //   sel_t[3:0] = sel; we_t = we

  // Notes on the sheet:
  //   Register File
  //   ALU
  //   Immediate Generator
  //   Sel
  //   0000
  //   1000
  //   0001
  //   0010
  //   0011
  //   0100
  //   0101
  //   1101
  //   0110
  //   0111
  //   RV32I ALU Operations
  //   Operation
  //   add-Summation
  //   sub-Subtraction
  //   sll - Shift left logical
  //   slt - Set less than
  //   sltu - Set Less than unsigned
  //   xor - eXclusive OR
  //   srl - Shift Right Logical
  //   sra - Shift right arithmetic
  //   or - logical OR
  //   and - logical AND
  //   *Sel composed of bit 6 of funct7 concatenated with funct3
endmodule

module ISplitter (
  input  [6:0] opcode,
  input  [4:0] rd,
  input  [2:0] funct3,
  input  [31:0] ins,
  input  [4:0] rs1,
  input  [11:0] imm11_0
);


  assign {ins[31:20], ins[14:12]} = {imm11_0, funct3};
  assign opcode = ins[6:0];
  assign rd = ins[11:7];
  assign rs1 = ins[19:15];
endmodule

module SSplitter (
  input  [6:0] opcode,
  input  [4:0] imm4_0,
  input  [2:0] funct3,
  input  [31:0] ins,
  input  [4:0] rs1,
  input  [4:0] rs2,
  input  [6:0] imm11_5
);


  assign {ins[31:25], ins[14:7]} = {imm11_5, funct3, imm4_0};
  assign opcode = ins[6:0];
  assign rs1 = ins[19:15];
  assign rs2 = ins[24:20];
endmodule

module USplitter (
  input  [6:0] opcode,
  input  [4:0] rd,
  input  [31:0] ins,
  input  [19:0] imm31_12
);


  assign ins[31:12] = imm31_12;
  assign opcode = ins[6:0];
  assign rd = ins[11:7];
endmodule

module JSplitter (
  input  [6:0] opcode,
  input  [4:0] rd,
  input  [7:0] imm19_12,
  input  imm11,
  input  [9:0] imm10_11,
  input  [31:0] ins,
  input  imm20
);


  assign ins[31:12] = {imm20, imm10_11, imm11, imm19_12};
  assign opcode = ins[6:0];
  assign rd = ins[11:7];
endmodule

module BSplitter (
  input  [6:0] opcode,
  input  imm11,
  input  [3:0] imm4_1,
  input  [2:0] funct3,
  input  [4:0] rs1,
  input  [4:0] rs2,
  input  [5:0] imm10_5,
  input  imm12,
  input  [31:0] ins
);


  assign {ins[31:25], ins[14:7]} = {imm12, imm10_5, funct3, imm4_1, imm11};
  assign opcode = ins[6:0];
  assign rs1 = ins[19:15];
  assign rs2 = ins[24:20];
endmodule

module RSplitter (
  input  [6:0] opcode,
  input  [4:0] rd,
  input  [2:0] funct3,
  input  [4:0] rs1,
  input  [4:0] rs2,
  input  [6:0] funct7,
  input  [31:0] ins
);


  assign {ins[31:25], ins[14:12]} = {funct7, funct3};
  assign opcode = ins[6:0];
  assign rd = ins[11:7];
  assign rs1 = ins[19:15];
  assign rs2 = ins[24:20];
endmodule
